// Logisim project pg09_from_brom_decode.circ as structural Verilog: 1 circuit, main circuit main
module main (
  input  in_1,
  input  in_2,
  input  in_3,
  input  in_4,
  input  in_5,
  input  in_6,
  input  in_7,
  input  in_8
);

  wire and_7_out, BIT0, BIT1, BIT2, BIT3, BIT4, BIT5;

  and and_1 (BIT0, in_1, in_2);
  and and_2 (BIT1, in_3, in_2);
  and and_3 (BIT2, in_5, in_2);
  and and_4 (BIT3, in_6, in_2);
  and and_5 (BIT4, in_7, in_2);
  and and_6 (BIT5, in_8, in_2);
  and and_7 (and_7_out, in_2, in_4);
  LED led_1 (.in(and_7_out));
  Hex_Digit_Display hex_digit_display_1 (.value({2'b00, BIT5, BIT4}));  // open: dp
  Hex_Digit_Display hex_digit_display_2 (.value({BIT3, BIT2, BIT1, BIT0}));  // open: dp

  // Other names for the same wires on the sheet: nBROMSEL = in_4; nFROMSEL = in_2; RB0 = in_1; RB1 = in_3; RB2 = in_5;
  //   RB3 = in_6; RB4 = in_7; RB5 = in_8

  // Notes on the sheet:
  //   Flash ROM select
  //   Bank number
endmodule
